# Fritzing sketch practice4-breadboard_photoreflector (saved by Fritzing 0.9.3b)
breadboards: 1

parts:
  パーツ1 = Arduino Uno (Rev3)
  U1 = TPR105 [package=TPR105]
  R1 = Resistor [tolerance=±5% resistance=330 package=THT]
  R2 = Resistor [tolerance=±5% resistance=47k package=THT]
  LED1 = LED - 5mm [color="Blue (470nm)" package="5 mm [THT]"]
  R3 = Resistor [tolerance=±5% resistance=470 package=THT]

nets:
  N1: パーツ1.A0, U1.C, R2.Pin_0
  N2: パーツ1.5V, R2.Pin_1
  N3: パーツ1.GND, U1.K, LED1.cathode
  N4: U1.A, R1.Pin_1
  N5: LED1.anode, R3.Pin_1

custom parts:
  TPR105: Reflective object sensor
